# Fritzing sketch Aircraft-Lighting_System (saved by Fritzing 0.9.6b)
breadboards: 1

parts:
  LED1 = LED - 5mm [color="Green (555nm)" current=0.030 package="5 mm [THT]"]
  LED2 = LED - 5mm [color="White (6500K)" current=0.030 package="5 mm [THT]"]
  LED3 = LED - 5mm [color="White (6500K)" current=0.030 package="5 mm [THT]"]
  LED4 = LED - 5mm [color="Red (633nm)" current=0.030 package="5 mm [THT]"]
  R1 = Resistor [tolerance=±5% resistance=220 package="0603 [SMD]"]
  R2 = Resistor [tolerance=±5% resistance=220 package="0603 [SMD]"]
  R3 = Resistor [tolerance=±5% resistance=220 package="0603 [SMD]"]
  R4 = Resistor [tolerance=±5% resistance=220 package="0603 [SMD]"]
  Part1 = Arduino Uno (Rev3)
  LED5 = LED - 5mm [color="Red (633nm)" current=0.030 package="5 mm [THT]"]
  LED6 = LED - 5mm [color="Red (633nm)" current=0.030 package="5 mm [THT]"]
  R5 = Resistor [tolerance=±5% resistance=220 package="0603 [SMD]"]

nets:
  N1: LED1.cathode, LED2.cathode, LED3.cathode, LED4.cathode, Part1.GND, LED5.cathode, LED6.cathode
  N2: LED1.anode, R3.Pin_1
  N3: LED2.anode, R1.Pin_0
  N4: LED3.anode, R4.Pin_1
  N5: LED4.anode, R2.Pin_0
  N6: R1.Pin_1, R4.Pin_0, Part1.D9_PWM
  N7: R2.Pin_1, Part1.D11_PWM/MOSI
  N8: R3.Pin_0, Part1.D5_PWM
  N9: Part1.D10_PWM/SS, R5.Pin_1
  N10: LED5.anode, LED6.anode, R5.Pin_0
