# Fritzing sketch Race_Light_System (saved by Fritzing 0.9.6b)
breadboards: 1

parts:
  LED1 = LED - 5mm [color="Red (633nm)" current=0.030 package="5 mm [THT]"]
  Part1 = Arduino Uno (Rev3)
  LED2 = LED - 5mm [color="Red (633nm)" current=0.030 package="5 mm [THT]"]
  LED3 = LED - 5mm [color="Red (633nm)" current=0.030 package="5 mm [THT]"]
  LED4 = LED - 5mm [color="Red (633nm)" current=0.030 package="5 mm [THT]"]
  LED5 = LED - 5mm [color="Red (633nm)" current=0.030 package="5 mm [THT]"]
  LED6 = LED - 5mm [color="Green (555nm)" current=0.030 package="5 mm [THT]"]
  LED7 = LED - 5mm [color="Green (555nm)" current=0.030 package="5 mm [THT]"]
  LED8 = LED - 5mm [color="Green (555nm)" current=0.030 package="5 mm [THT]"]
  LED9 = LED - 5mm [color="Green (555nm)" current=0.030 package="5 mm [THT]"]
  LED10 = LED - 5mm [color="Green (555nm)" current=0.030 package="5 mm [THT]"]
  R1 = Resistor [tolerance=±5% resistance=220 package="0603 [SMD]"]
  R2 = Resistor [tolerance=±5% resistance=220 package="0603 [SMD]"]
  R3 = Resistor [tolerance=±5% resistance=220 package="0603 [SMD]"]
  R4 = Resistor [tolerance=±5% resistance=220 package="0603 [SMD]"]
  R5 = Resistor [tolerance=±5% resistance=220 package="0603 [SMD]"]
  LED11 = LED - 5mm [color="Yellow (595nm)" current=0.030 package="5 mm [THT]"]
  LED12 = LED - 5mm [color="Yellow (595nm)" current=0.030 package="5 mm [THT]"]
  LED13 = LED - 5mm [color="Yellow (595nm)" current=0.030 package="5 mm [THT]"]
  LED14 = LED - 5mm [color="Yellow (595nm)" current=0.030 package="5 mm [THT]"]
  LED15 = LED - 5mm [color="Yellow (595nm)" current=0.030 package="5 mm [THT]"]
  R6 = Resistor [tolerance=±5% resistance=220 package="0603 [SMD]"]
  R7 = Resistor [tolerance=±5% resistance=220 package="0603 [SMD]"]
  R8 = Resistor [tolerance=±5% resistance=220 package="0603 [SMD]"]
  R9 = Resistor [tolerance=±5% resistance=220 package="0603 [SMD]"]
  R10 = Resistor [tolerance=±5% resistance=220 package="0603 [SMD]"]

nets:
  N1: LED1.cathode, Part1.GND, LED2.cathode, LED3.cathode, LED4.cathode, LED5.cathode, LED6.cathode, LED7.cathode, LED8.cathode, LED9.cathode, LED10.cathode, LED11.anode, LED12.anode, LED13.anode, LED14.anode, LED15.anode
  N2: LED1.anode, Part1.D2, R1.Pin_1
  N3: Part1.D8, R7.Pin_0
  N4: Part1.D9_PWM, R8.Pin_1
  N5: Part1.D10_PWM/SS, R9.Pin_1
  N6: Part1.D11_PWM/MOSI, R10.Pin_1
  N7: Part1.D12/MISO, LED11.cathode, LED12.cathode, LED13.cathode, LED14.cathode, LED15.cathode
  N8: Part1.D3_PWM, LED2.anode, R2.Pin_1
  N9: Part1.D4, LED3.anode, R3.Pin_1
  N10: Part1.D5_PWM, LED4.anode, R4.Pin_0
  N11: Part1.D6_PWM, LED5.anode, R5.Pin_0
  N12: Part1.D7, R6.Pin_0
  N13: LED6.anode, R6.Pin_1
  N14: LED7.anode, R7.Pin_1
  N15: LED8.anode, R8.Pin_0
  N16: LED9.anode, R9.Pin_0
  N17: LED10.anode, R10.Pin_0
