# Fritzing sketch Automatic_Light-Bulb_Photoresistor-Scheme (saved by Fritzing 0.9.6b)
breadboards: 1

parts:
  Part1 = Arduino Uno (Rev3)
  R1 = Photocell (LDR) [package=THT]
  R2 = Resistor [tolerance=±5% power=0.25 resistance=10k package=THT]
  KY-1 = Keyes Relay [package=THT]
  BULB1 = Incandescent light bulb small [package="bulb sm"]
  Part2 = Lilypad Battery Connect

nets:
  N1: Part1.A0, R1.pin_1, R2.Pin_0
  N2: Part1.D3_PWM, KY-1.signal
  N3: Part1.5V, R1.pin_0, KY-1.power
  N4: Part1.GND, R2.Pin_1, KY-1.ground
  N5: KY-1.C, Part2.-
  N6: KY-1.NO, BULB1.2
  N7: BULB1.1, Part2.+

custom parts:
  Keyes Relay: The Keyes 5V relay module is suitable for SCM development, home appliance control. It uses a 5V~12V TIL control signal which can control DC / AC signal.
