# Fritzing sketch Automatic_Light_With_BH1750-Sensor_Scheme (saved by Fritzing 0.9.6b)
breadboards: 1

parts:
  Part1 = BH1750
  Part2 = Arduino Uno (Rev3)
  KY-1 = Keyes Relay [package=THT]
  Part3 = Lilypad Battery Connect
  LED1 = LEDs [package=led10mm]

nets:
  VCC: Part1.VCC, Part2.5V, KY-1.power
  GND: Part1.GND, Part2.GND, KY-1.ground
  N1: Part1.SCL, Part2.A5/SCL
  N2: Part1.SDA, Part2.A4/SDA
  N3: Part2.D3_PWM, KY-1.signal
  N4: KY-1.C, Part3.+
  N5: KY-1.NO, LED1.C
  N6: Part3.-, LED1.A

notes:
  Power Plug

custom parts:
  BH1750: Light Sensor
  Keyes Relay: The Keyes 5V relay module is suitable for SCM development, home appliance control. It uses a 5V~12V TIL control signal which can control DC / AC signal.
  LEDs: LEDs Standard schematic elements and footprints for 5mm, 3mm, 1206, and 0603 sized LEDs. 5mm - Spark Fun Electronics SKU : COM-00529 (and others)
