# Fritzing sketch DHT11-LCD-Scheme (saved by Fritzing 0.9.6b)
breadboards: 1

parts:
  Part1 = Arduino Uno (Rev3)
  LCD2004-I2C1 = LCD2004-I2C
  DHT1 = DHT11 Humitidy and Temperature Sensor
  R1 = Resistor [tolerance=±5% resistance=4.7k package="1206 [SMD]"]

nets:
  N1: Part1.A4/SDA, LCD2004-I2C1.SDA
  N2: Part1.A5/SCL, LCD2004-I2C1.SCL
  N3: Part1.D2, DHT1.DATA, R1.Pin_1
  5V: Part1.5V, LCD2004-I2C1.VCC, DHT1.VDD, R1.Pin_0
  GND: Part1.GND, LCD2004-I2C1.GND, DHT1.GND

notes:
  Use 4.7K-10KΩ resistor

custom parts:
  LCD2004-I2C: A standard character display with 4x20 characters. Comes in many colors with LCM2004 IIC attached.
  DHT11 Humitidy and Temperature Sensor: DHT11 Humidity and Temperature Sensor
