# Fritzing sketch Water_Level-Sensor-Scheme (saved by Fritzing 0.9.6b)
breadboards: 1

parts:
  Water_Level_Sensor1 = Water Level Sensor
  Part1 = Arduino Uno (Rev3)
  R1 = Resistor [tolerance=±5% power=0.25 resistance=220 package=THT]
  LED1 = LED - 5mm [color="Red (633nm)" current=0.030 package="5 mm [THT]"]

nets:
  N1: Water_Level_Sensor1.SIG, Part1.A0
  N2: Water_Level_Sensor1.VCC, Part1.D3_PWM
  GND: Water_Level_Sensor1.GND, Part1.GND, R1.Pin_0
  N3: Part1.D13/SCK, LED1.anode
  N4: R1.Pin_1, LED1.cathode

custom parts:
  Water Level Sensor: A water level sensor. This sensor operates at 3V to 5V. The Sig (signal) pin outputs an analogue signal that is in proportion to the amount of water in contact with the sensor.
