# Fritzing sketch lm35-scheme (saved by Fritzing 0.9.6b)
breadboards: 1

parts:
  T1 = LM35 Temperature Sensor [package="TO92 [THT]"]
  Part1 = Arduino Uno (Rev3)
  LCD2004-I2C1 = LCD2004-I2C

nets:
  N1: T1.Vout, Part1.A0
  GND: T1.GND, Part1.GND, LCD2004-I2C1.GND
  N2: Part1.A4/SDA, LCD2004-I2C1.SDA
  N3: Part1.A5/SCL, LCD2004-I2C1.SCL
  5V: Part1.5V, LCD2004-I2C1.VCC

custom parts:
  LCD2004-I2C: A standard character display with 4x20 characters. Comes in many colors with LCM2004 IIC attached.
